# Fritzing sketch circuit_diagram_exploration (saved by Fritzing 0.9.3b)
breadboards: 1

parts:
  Part1 = Arduino Mega 2560 (Rev3)
  M1 = fc-51 [package=THT]
  M2 = fc-51 [package=THT]
  M3 = fc-51 [package=THT]
  M4 = fc-51 [package=THT]
  J2 = Basic Servo
  J3 = Basic Servo
  J4 = Basic Servo
  M5 = DC Motor
  U1 = 2-Channel 5v Relay Shield [package=relay-2ch5v10a]
  SG1 = Buzzer 12mm [package=buzzer-ccv]
  VCC1 = Battery block 9V  # not connected
  VCC2 = 4 x AAA Battery Mount  # not connected
  J1 = Basic Servo
  BAT2 = 12 battery [package=battery]

nets:
  GND: Part1.GND, M1.pin2, M2.pin2, M3.pin2, M4.pin2, J2.gnd, J3.gnd, J4.gnd, U1.GND, SG1.1, J1.gnd
  N1: Part1.D12_PWM, U1.IN2
  N2: Part1.D11_PWM, U1.IN1
  5V: Part1.5V, M1.pin3, M2.pin3, M3.pin3, M4.pin3, U1.VCC
  N3: Part1.D2_PWM, J2.pulse
  N4: Part1.D3_PWM, J1.pulse
  N5: Part1.D4_PWM, J4.pulse
  N6: Part1.D5_PWM, J3.pulse
  N7: Part1.D22, M1.pin1
  N8: Part1.D23, M2.pin1
  N9: Part1.D24, M3.pin1
  N10: Part1.D25, M4.pin1
  N11: Part1.D35, SG1.2
  N12: M5.pin_1, U1.K1-In
  N13: M5.pin_2, U1.K2-In
  N14: U1.K1-Off, U1.K2-Off, BAT2.-
  N15: U1.K1-On, U1.K2-On, BAT2.+

custom parts:
  2-Channel 5v Relay Shield: 2 Channel 5v Relay Shield w. 2x SPD-06VDC-SD-C
  12 battery: 12V lead acid type battery, like the Husqvarna YTH2448 12V 35AH battery. This is the mini version 1/4 the size of the actual battery to be closer to typical breadboard parts (around 2in wide rathher than 7in). The pads in pcb are sized to accomidate up to 14ga wire (as these batterys will deliver high currents.)
